# Fritzing sketch Arduino L298N (saved by Fritzing 0.9.5d)

parts:
  M3 = gear-motor
  L298N1 = L298N DC motor driver
  BAT1 = BC9VPC [package=bc9vpc]
  M4 = gear-motor
  HC-SR04_Sensor_1 = HC-SR04 Ultrasonic Distance Sensor
  Part1 = Arduino Uno (Rev3)

nets:
  N1: M3.pin_1, L298N1.OUT4
  N2: M3.pin_2, L298N1.OUT3
  N3: L298N1.OUT1, M4.pin_2
  N4: L298N1.OUT2, M4.pin_1
  N5: L298N1.12V, BAT1.V+
  GND: L298N1.GND, HC-SR04_Sensor_1.GND, Part1.GND
  5V: L298N1.5V, HC-SR04_Sensor_1.VCC, Part1.5V
  N6: L298N1.ENA, Part1.D10_PWM/SS
  N7: L298N1.ENB, Part1.D5_PWM
  N8: L298N1.IN1, Part1.D9_PWM
  N9: L298N1.IN2, Part1.D8
  N10: L298N1.IN3, Part1.D7
  N11: L298N1.IN4, Part1.D6_PWM
  N12: HC-SR04_Sensor_1.TRIG, Part1.D3_PWM
  N13: HC-SR04_Sensor_1.ECHO, Part1.D2

custom parts:
  L298N DC motor driver: 2x DC motor driver with 78M05 positive voltage regulator (7..35 V) L298N: max 46 V, 2 A Set 5 V Enable jumper to enable 5 V regultor (needed for the L298N) and +5 V output at screw terminal or supply external +5 V at screw terminal Set ENA and/or ENB to +5 V to enable motor permanently or supply ENA and/or ENB with PWM signal IN1 and IN2 set rotation directory for motor A (OUT1/OUT2) IN2 and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
